# Fritzing sketch main_architecture (saved by Fritzing 0.9.1b)

parts:
  Componente1 = Arduino Mega 2560 (Rev3)
  Componente2 = Arduino Mega 2560 (Rev3)
  U1 = RS485 [package=so08]
  U2 = RS485 [package=so08]
  X2 = USB Connectors [package=usb-a-s]  # not connected
  Componente3 = Arduino Mega 2560 (Rev3)  # not connected

nets:
  N1: Componente1.D19/RX1, U2.GND
  N2: Componente1.D18/TX1, U2.VCC
  N3: Componente1.5V, U2.DI
  N4: Componente1.GND, U2.RO
  N5: Componente1.D3_PWM, U2.A, U2.B
  N6: Componente2.D19/RX1, U1.GND
  N7: Componente2.D18/TX1, U1.VCC
  N8: Componente2.5V, U1.DI
  N9: Componente2.GND, U1.RO
  N10: Componente2.D3_PWM, U1.A, U1.B
  N11: U1._RE, U2._RE
  N12: U1.DE, U2.DE

notes:
  DI - DE - RE - RO
  8 7 6 5
  1 2 3 4
  GND A B VCC
  1 => OMRON 5V 240V solid state relay 2A, output with resistance type fuse 240V 2A.
  2 => size: 57*55*25 (length * width * height) net weight: 40g
  3 => the input power supply: 5V DC (160MA)
  4 => the input control signal voltage:
  (0-2.5V the state of low level relay OFF)
  (3.3-5V high level relay ON)
  -------------------------
  The static current voltage version of the working current of trigger voltage, trigger current:
  - 4 way 5V 0mA 48mA 3.3-5V 2mA
  DI - Data IN (to Arduino TX PIN)
  DE - Data Enable (to Arduino ENABLE_PIN)
  RE - Receive Enable (to Arduino ENABLE_PIN)
  RO - Receive OUT (to Arduino RX PIN)
  A, B - RS485 pair
  BUS RS485
  References:
  - https://arduino-info.wikispaces.com/SoftwareSerialRS485Example
  - http://www.gammon.com.au/forum/?id=11428
  USB ("source Power" references):
  Signal
  5 V DC
  Max. voltage
  5.00±0.25 V (pre-3.0)
  5.00+0.25
  −0.55 V (USB 3.0)
  Max. current
  0.5A (USB 2.0)
  0.9A (USB 3.0)
  Up to 5A (USB 3.1)
  => OMRON 5 V solid state relays each channel 240 V 2 A, output with resistive fuse 250 V 2 A.
  => SSR Output (each channel):
  => Load voltage range: 75 to 264VAC (50/60Hz).
  => Load current: 0.1 to 2 AMP.
  => Power supply:5VDC / 160mA .
  => Input control signal voltage:
  - 0V - 0.5V Low stage (SSR is OFF),
  - 0.5V - 2.5V (unknown state).
  - 2.5V - 20V High state (SSR is ON).
  => Size: 138 x 71 x 25 mm ( L*W*H).
  => SSR Spec.:
  - Manufacturer: OMRON
  - Part number: G3MB-202P, 5V version.
  - Isolation: Phototriac.
  - Zero cross: Yes.
  - Rated output load: 2A at 100 to 240VAC.(50/60Hz).
  => Load type: General purpose.
  Output voltage: AC 24-380V.
  Output current: 40A.
  Input voltage: DC 4-32V.
  Trigger current: 12.0mA max
  Leakage current: 5mA max
  Control Method: zero cross
  Mounting Method: Bolts fixed.
  Size:6.5cm x 4.5cm x 2.2cm - 2.56inch x 1.77inch x 0.87inch.
  Operating Voltage
  5V
  Input Voltage (recommended)
  7-12V
  Input Voltage (limit)
  6-20V
  DC Current per I/O Pin
  20 mA
  DC Current for 3.3V Pin
  50 mA
  Power The Mega 2560 can be powered via the USB connection or with an external power supply. The power source is selected automatically.
  External (non-USB) power can come either from an AC-to-DC adapter (wall-wart) or battery. The adapter can be connected by plugging a 2.1mm center-positive plug into the board's power jack. Leads from a battery can be inserted in the GND and Vin pin headers of the POWER connector.
  The board can operate on an external supply of 6 to 20 volts. If supplied with less than 7V, however, the 5V pin may supply less than five volts and the board may become unstable. If using more than 12V, the voltage regulator may overheat and damage the board. The recommended range is 7 to 12 volts.
  The power pins are as follows:
  Vin. The input voltage to the board when it's using an external power source (as opposed to 5 volts from the USB connection or other regulated power source). You can supply voltage through this pin, or, if supplying voltage via the power jack, access it through this pin.
  5V. This pin outputs a regulated 5V from the regulator on the board. The board can be supplied with power either from the DC power jack (7 - 12V), the USB connector (5V), or the VIN pin of the board (7-12V). Supplying voltage via the 5V or 3.3V pins bypasses the regulator, and can damage your board. We don't advise it.
  3V3. A 3.3 volt supply generated by the on-board regulator. Maximum current draw is 50 mA.
  GND. Ground pins.
  IOREF. This pin on the board provides the voltage reference with which the microcontroller operates. A properly configured shield can read the IOREF pin voltage and select the appropriate power source or enable voltage translators on the outputs for working with the 5V or 3.3V.
  Input and Output
  => Each of the 54 digital pins on the Mega can be used as an input or output, using pinMode(), digitalWrite(), and digitalRead() functions. They operate at 5 volts. Each pin can provide or receive 20 mA as recommended operating condition and has an internal pull-up resistor (disconnected by default) of 20-50 k ohm. A maximum of 40mA is the value that must not be exceeded to avoid permanent damage to the microcontroller.
